# Fritzing sketch Esquema básico - Braço + MPU 9250 (saved by Fritzing 0.9.3b)
breadboards: 1

parts:
  10DOF1 = CJMCU-10DOF [form="♀ (female)" package=THT]
  Componente1 = Arduino Uno (Rev3)  # not connected
  Componente2 = Arduino Sensor Shield v5.0
  J1 = Basic Servo
  Componente3 = Bluetooth HC-05 Macho

nets:
  +3V3: 10DOF1.+3V3, Componente2.+5V#51, Componente2.3.3V, Componente3.VCC
  GND: 10DOF1.GND, Componente2.GND#54, Componente2.GND#62, Componente3.GND
  N1: 10DOF1.SCL, Componente2.A5
  N2: 10DOF1.SDA, Componente2.A4
  N3: Componente2.D10, Componente3.RXD
  N4: Componente2.D11, Componente3.TXD
  N5: Componente2.D4, J1.pulse
  N6: Componente2.+5V#90, J1.vcc
  N7: Componente2.GND#144, J1.gnd

notes:
  4x Servos SG90
  * Portas 4 a 7 Digital IO

custom parts:
  CJMCU-10DOF: Placa CJMCU 10DOF basada en conjunto de acelerómetro+giroscopios+magnetómetro MPU-9250 y un barómetro BMP180
